# Fritzing sketch venkman (saved by Fritzing 0.9.3b)
breadboards: 2

parts:
  D1 = LED_BARGRAPH_10 [package=led_bargaph_10]
  R1 = Resistor [tolerance=±5% resistance=220 package="0805 [SMD]"]
  D2 = LED_BARGRAPH_10 [package=led_bargaph_10]
  R2 = Resistor [tolerance=±5% resistance=220 package="0805 [SMD]"]
  IC1 = SHIFT REGISTER [package=dil16]
  IC2 = SHIFT REGISTER [package=dil16]
  IC3 = SHIFT REGISTER [package=dil16]
  D3 = LED_BARGRAPH_10 [package=led_bargaph_10]
  D4 = LED_BARGRAPH_10 [package=led_bargaph_10]
  R3 = Resistor [tolerance=±5% resistance=220 package="0805 [SMD]"]
  R4 = Resistor [tolerance=±5% resistance=220 package="0805 [SMD]"]
  IC4 = SHIFT REGISTER [package=dil16]
  IC5 = SHIFT REGISTER [package=dil16]
  Part2 = Arduino Mega ADK (Rev3)
  LED1 = smd LED [color="Red (633nm)" package="0603 [SMD]"]
  IC6 = SHIFT REGISTER [package=dil16]
  R5 = Resistor [tolerance=±5% resistance=220 package="0805 [SMD]"]
  LED2 = smd LED [color="Red (633nm)" package="0603 [SMD]"]
  LED3 = smd LED [color="Red (633nm)" package="0603 [SMD]"]
  LED4 = smd LED [color="Red (633nm)" package="0603 [SMD]"]
  R6 = Resistor [tolerance=±5% resistance=220 package="0805 [SMD]"]
  R7 = Resistor [tolerance=±5% resistance=220 package="0805 [SMD]"]
  R8 = Resistor [tolerance=±5% resistance=220 package="0805 [SMD]"]

nets:
  N1: D1.A_A, D1.B_A, D1.C_A, D1.D_A, D1.E_A, D1.F_A, D1.G_A, D1.H_A, D1.I_A, D1.J_A, R1.Pin_0
  N2: D1.J_C, IC2.QB
  N3: D1.I_C, IC2.QA
  N4: D1.H_C, IC1.QH
  N5: D1.G_C, IC1.QG
  N6: D1.F_C, IC1.QF
  N7: D1.E_C, IC1.QE
  N8: D1.D_C, IC1.QD
  N9: D1.C_C, IC1.QC
  N10: D1.B_C, IC1.QB
  N11: D1.A_C, IC1.QA
  GND: R1.Pin_1, R2.Pin_1, IC1.GND, IC2.GND, IC3.GND, R3.Pin_1, R4.Pin_1, IC4.GND, IC5.GND, IC6.GND, R5.Pin_0, R6.Pin_0, R7.Pin_0, R8.Pin_0
  N12: D2.A_A, D2.B_A, D2.C_A, D2.D_A, D2.E_A, D2.F_A, D2.G_A, D2.H_A, D2.I_A, D2.J_A, R2.Pin_0
  N13: D2.J_C, IC3.QD
  N14: D2.I_C, IC3.QC
  N15: D2.H_C, IC3.QB
  N16: D2.G_C, IC3.QA
  N17: D2.F_C, IC2.QH
  N18: D2.E_C, IC2.QG
  N19: D2.D_C, IC2.QF
  N20: D2.C_C, IC2.QE
  N21: D2.B_C, IC2.QD
  N22: D2.A_C, IC2.QC
  VCC: IC1.SCL, IC1.VCC, IC2.SCL, IC2.VCC, IC3.SCL, IC3.VCC, IC4.SCL, IC4.VCC, IC5.SCL, IC5.VCC, Part2.5V, IC6.SCL, IC6.VCC
  N23: IC1.SCK, Part2.D12_PWM
  N24: IC1.RCK, Part2.D11_PWM
  N25: IC1.G, IC2.G, IC3.G, IC4.G, IC5.G, Part2.GND, IC6.G
  N26: IC1.SER, Part2.D13_PWM
  N27: IC2.SCK, Part2.D8_PWM
  N28: IC2.RCK, Part2.D9_PWM
  N29: IC2.SER, Part2.D10_PWM
  N30: IC3.QE, D3.A_C
  N31: IC3.QF, D3.B_C
  N32: IC3.QG, D3.C_C
  N33: IC3.QH, D3.D_C
  N34: IC3.SCK, Part2.D5_PWM
  N35: IC3.RCK, Part2.D6_PWM
  N36: IC3.SER, Part2.D7_PWM
  N37: D3.A_A, D3.B_A, D3.C_A, D3.D_A, D3.E_A, D3.F_A, D3.G_A, D3.H_A, D3.I_A, D3.J_A, R3.Pin_0
  N38: D3.J_C, IC4.QF
  N39: D3.I_C, IC4.QE
  N40: D3.H_C, IC4.QD
  N41: D3.G_C, IC4.QC
  N42: D3.F_C, IC4.QB
  N43: D3.E_C, IC4.QA
  N44: D4.A_A, D4.B_A, D4.C_A, D4.D_A, D4.E_A, D4.F_A, D4.G_A, D4.H_A, D4.I_A, D4.J_A, R4.Pin_0
  N45: D4.J_C, IC5.QH
  N46: D4.I_C, IC5.QG
  N47: D4.H_C, IC5.QF
  N48: D4.G_C, IC5.QE
  N49: D4.F_C, IC5.QD
  N50: D4.E_C, IC5.QC
  N51: D4.D_C, IC5.QB
  N52: D4.C_C, IC5.QA
  N53: D4.B_C, IC4.QH
  N54: D4.A_C, IC4.QG
  N55: IC4.SCK, Part2.D2_PWM
  N56: IC4.RCK, Part2.D3_PWM
  N57: IC4.SER, Part2.D4_PWM
  N58: IC5.SCK, Part2.D14/TX3
  N59: IC5.RCK, Part2.D0/RX0
  N60: IC5.SER, Part2.D1/TX0
  N61: Part2.D17/RX2, IC6.SCK
  N62: Part2.D16/TX2, IC6.RCK
  N63: Part2.D15/RX3, IC6.SER
  N64: LED1.cathode, IC6.QA
  N65: LED1.anode, R5.Pin_1
  N66: IC6.QB, LED2.cathode
  N67: IC6.QC, LED3.cathode
  N68: IC6.QD, LED4.cathode
  N69: LED2.anode, R6.Pin_1
  N70: LED3.anode, R7.Pin_1
  N71: LED4.anode, R8.Pin_1
